# Fritzing sketch arrow (saved by Fritzing 0.9.5d)

parts:
  Part1 = Adafruit Motor Bonnet [part_number="Adafruit #4280"]
  MCU1 = Raspberry Pi Zero
  M2 = Stepper Motor - Bipolar
  JACK1 = 2.1mm Barrel Jack with Terminal Block
  MOTOR1 = Adafruit Gear-Reduced Stepper Motor (small)
  SparkFun_IMU_Breakout_ICM-1 = SparkFun IMU Breakout ICM-20948 [part_number=15335]
  LED2 = RGB LED (com. cathode, rbg) [package="5 mm [THT]"]
  Part6 = VERTER 5V USB Buck-Boost
  Part7 = Adafruit DS3231 [part_number="Adafruit #3013"]
  Part5 = OLED Monochrome 128x64 0.96 inch [part_number=326]

nets:
  N1: Part1.SDA, MCU1.pin_3, SparkFun_IMU_Breakout_ICM-1.SDA/SDI_VIN, Part7.SDA, Part5.MOSI_SDA
  N2: Part1.SCL, MCU1.pin_5, SparkFun_IMU_Breakout_ICM-1.SCL/SCLK_VIN, Part7.SCL, Part5.SCLK_SCK
  N3: Part1.M2A, M2.D
  N4: Part1.M2B, M2.B
  N5: Part1.M1B, M2.C
  N6: Part1.M1A, M2.A
  N7: Part1.M4A, MOTOR1.BLUE
  N8: Part1.M4B, MOTOR1.PINK
  GND: Part1.GND, MCU1.pin_6, MCU1.pin_9, MCU1.pin_14, MCU1.pin_34, JACK1.NEG, MOTOR1.YELLOW, SparkFun_IMU_Breakout_ICM-1.GND, LED2.common_cathode, Part6.GND, Part7.GND, Part5.GND
  N9: Part1.M3B, MOTOR1.ORANGE
  N10: Part1.M3A, MOTOR1.RED
  N11: Part1.VMOTOR, MCU1.pin_2, MCU1.pin_4, JACK1.POS, Part6.VIN
  VIN: Part1.5.0V, SparkFun_IMU_Breakout_ICM-1.VIN, LED2.blue_anode, Part6.5.0V, Part7.Vin, Part5.VIN
  N12: Part1.GPIO18, LED2.green_anode

custom parts:
  Adafruit Motor Bonnet: Let your robotic dreams come true with the new DC+Stepper Motor Bonnet from Adafruit. This Raspberry Pi add-on is perfect for any motion project as it can drive up to 4 DC or 2 Stepper motors with full PWM speed control. We basically took our super-popular DC+Stepper Motor HAT and squeezed it down and made it fully assembled - plug and play ready to go, no soldering required!
  Adafruit Gear-Reduced Stepper Motor (small): Adafruit gear-reduction stepper motor (small)
  SparkFun IMU Breakout ICM-20948: The SparkFun 9DoF IMU Breakout incorporates all the amazing features of Invensense's ICM-20948 into a Qwiic-enabled breakout board complete with a logic shifter and broken out GPIO pins for all your motion sensing needs. The ICM-20948 itself is an extremely low powered, I2C and SPI enabled 9-axis motion tracking device that is ideally suited for smartphones, tablets, wearable sensors, and IoT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
  VERTER 5V USB Buck-Boost: VERTER can take battery voltages from 3-12VDC and output a nice 5V DC, which makes it a perfect universal power supply for your portable project! Where Verter really shines is when you have a battery or power range that can fluctuate a lot, or you don't know what you'll end up using.
  Adafruit DS3231: The datasheet for the DS3231 explains that this part is an "Extremely Accurate I²C-Integrated RTC/TCXO/Crystal". And, hey, it does exactly what it says on the tin! This Real Time Clock (RTC) is the most precise you can get in a small, low power package. Most RTCs use an external 32kHz timing crystal that is used to keep time with low current draw. And that's all well and good, but those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
  OLED Monochrome 128x64 0.96 inch: These displays are small, only about 1" diameter, but very readable due to the high contrast of an OLED display. This display is made of 128x64 individual white OLED pixels, each one is turned on or off by the controller chip. Because the display makes its own light, no backlight is required. This reduces the power required to run the OLED and is why the display has such high contrast; we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
